# Fritzing sketch joystick new Sketch 1 (saved by Fritzing 1.0.0rc)

parts:
  VCC1 = 10440 Clips
  Mod1 = KY-023 Dual Axis Joystick Module [package="Breakout board"]
  M1 = 0.9v-5V booster usb output
  S2 = Toggle Switch [package=THT]
  U1 = ESP32-38PinWide [part_number=ESP32-38PinWide]

nets:
  N1: VCC1.+, S2.L1
  GND: Mod1.GND, U1.GND
  +5V: Mod1.+5V, M1.pin3, U1.VIN
  N2: Mod1.VRx, U1.GPIO32
  N3: Mod1.VRy, U1.GPIO33
  N4: Mod1.SW, U1.GPIO21
  N5: M1.pin1, M1.pin4, U1.GPIO11
  N6: M1.pin2, S2.COM

custom parts:
  10440 Clips: Keystone #82 Through hole battery clip
  KY-023 Dual Axis Joystick Module: KY-023 Dual-Axis Joystick Module.
  0.9v-5V booster usb output: 0.9 V ~ 5 V up 5 V DC - DC booster module.
  ESP32-38PinWide: Generic 38-Pin ESP32 with wide format (only access to one side of pins on a breadboard) based on Stephen Lilley's HiLetgo ESP-WROOM-32 ESP32 ESP-32S Development Board.
