# Fritzing sketch omni robot circuit diagram new updated (saved by Fritzing 1.0.0rc)
breadboards: 1

parts:
  U1 = ESP32-38PinWide [part_number=ESP32-38PinWide]
  U2 = LIPO-2000mAh [package=lipo-2000]
  U3 = LIPO-2000mAh [package=lipo-2000]
  U4 = LIPO-2000mAh [package=lipo-2000]
  A1 = drv-1012
  A2 = drv-1012
  A3 = drv-1012
  M1 = RioRand LM2596
  M2 = DC Motor [voltage_(max)=6V voltage_(min)=3V]
  M3 = DC Motor [voltage_(max)=6V voltage_(min)=3V]
  M4 = DC Motor [voltage_(max)=6V voltage_(min)=3V]
  S1 = Pushbutton [package=THT]

nets:
  N1: U1.3.3, A1.Pin_3, A1.Pin_7, A2.Pin_3, A2.Pin_7, A3.Pin_3, A3.Pin_7
  N2: U1.GPIO25, A3.Pin_8
  N3: U1.GPIO26, A3.Pin_4
  N4: U1.GPIO11, A1.Pin_1, A1.Pin_2, A1.Pin_6, A2.Pin_1, A2.Pin_2, A2.Pin_6, A3.Pin_1, A3.Pin_2, A3.Pin_6
  N5: U1.VIN, A1.Pin_5, A2.Pin_5, A3.Pin_5, M1.Pin_3
  N6: U1.GPIO16, A1.Pin_8
  N7: U1.GPIO17, A1.Pin_4
  N8: U1.GPIO22, A2.Pin_4
  N9: U1.GPIO23, A2.Pin_8
  N10: U2.+, S1.leg0
  N11: U2.-, U3.+
  N12: U3.-, U4.+
  N13: U4.-, M1.Pin_2
  N14: A1.Pin_9, M4.pin_2
  N15: A1.Pin_10, M4.pin_1
  N16: A1.Pin_11, M1.Pin_4
  N17: A1.Pin_12, A2.Pin_12
  N18: A2.Pin_9, M2.pin_2
  N19: A2.Pin_10, M2.pin_1
  N20: A3.Pin_9, M3.pin_2
  N21: A3.Pin_10, M3.pin_1
  N22: M1.Pin_1, S1.leg1

custom parts:
  ESP32-38PinWide: Generic 38-Pin ESP32 with wide format (only access to one side of pins on a breadboard) based on Stephen Lilley's HiLetgo ESP-WROOM-32 ESP32 ESP-32S Development Board.
  drv-1012: .The BTS7960 is a fully integrated high current H bridge module for motor drive applications.
